// Logisim project flip_flop.circ as structural Verilog: 1 circuit, main circuit main
module main (
  input  in_1,
  input  in_2,
  input  in_3,
  input  in_4,
  input  in_5,
  output out_6,
  output out_7,
  output out_8,
  output out_9
);

  D_Flip_Flop d_ff_1 (.D(in_1), .clk(in_2), .Q(out_6), .Qn(out_7));  // open: preset, reset
  J_K_Flip_Flop j_k_ff_1 (.J(in_3), .K(in_4), .clk(in_5), .Q(out_8), .Qn(out_9));  // open: preset, reset
endmodule
