// Logisim project D_74.circ as structural Verilog: 1 circuit, main circuit main
module main (
  input  A,
  input  B,
  input  C,
  input  D,
  input  in_5,
  output out_6,
  output out_7,
  output out_8,
  output out_9
);

  wire clk_out;

  Clock clk (.out(clk_out));
  _7474 u_7474_1 (
    .pin2(B), .pin3(clk_out), .pin5(out_7), .pin12(A), .pin11(clk_out), .pin9(out_6));  // open: pin1, pin4, pin6, pin13, pin10, pin8
  _7474 u_7474_2 (
    .pin2(D), .pin3(clk_out), .pin4(in_5), .pin5(out_9), .pin12(C), .pin11(clk_out), .pin9(out_8));  // open: pin1, pin6, pin13, pin10, pin8
endmodule
