// Logisim project D_flip_flop_reg.circ as structural Verilog: 1 circuit, main circuit main
module main (
  input  a,
  input  b,
  input  c,
  input  d,
  input  reset,
  output Qa,
  output Qb,
  output Qc,
  output Qd
);

  wire clock_1_out;

  Clock clock_1 (.out(clock_1_out));
  D_Flip_Flop d_ff_1 (.D(a), .clk(clock_1_out), .Q(Qa), .reset(reset));  // open: Qn, preset
  D_Flip_Flop d_ff_2 (.D(b), .clk(clock_1_out), .Q(Qb), .reset(reset));  // open: Qn, preset
  D_Flip_Flop d_ff_3 (.D(c), .clk(clock_1_out), .Q(Qc), .reset(reset));  // open: Qn, preset
  D_Flip_Flop d_ff_4 (.D(d), .clk(clock_1_out), .Q(Qd), .reset(reset));  // open: Qn, preset
endmodule
