// Logisim project D_flip_flop_reg_with_pin.circ as structural Verilog: 1 circuit, main circuit main
module main (
  input  A,
  input  B,
  input  C,
  input  D,
  input  clk,
  output Qa,
  output out_7,
  output out_8,
  output out_9
);

  wire AD_pin1, AD_pin2, AD_pin4, n7400_1_pin3, n7400_1_pin6, n7400_1_pin8, n7400_1_pin11, n7400_2_pin1,
       n7400_2_pin2, n7400_2_pin4, n7400_3_pin1, n7400_3_pin2, n7400_3_pin4, n7400_4_pin1, n7400_4_pin2,
       n7400_4_pin4;

  _7400 u_7400_1 (
    .pin1(C), .pin2(C), .pin3(n7400_1_pin3), .pin4(D), .pin5(D), .pin6(n7400_1_pin6), .pin13(A), .pin12(A),
    .pin11(n7400_1_pin11), .pin10(B), .pin9(B), .pin8(n7400_1_pin8));
  _7400 AD (
    .pin1(AD_pin1), .pin2(AD_pin2), .pin3(Qa), .pin4(AD_pin4), .pin5(Qa), .pin6(AD_pin2), .pin13(A),
    .pin12(clk), .pin11(AD_pin1), .pin10(n7400_1_pin11), .pin9(clk), .pin8(AD_pin4));
  _7400 u_7400_2 (
    .pin1(n7400_2_pin1), .pin2(n7400_2_pin2), .pin3(out_7), .pin4(n7400_2_pin4), .pin5(out_7),
    .pin6(n7400_2_pin2), .pin13(B), .pin12(clk), .pin11(n7400_2_pin1), .pin10(n7400_1_pin8), .pin9(clk),
    .pin8(n7400_2_pin4));
  _7400 u_7400_3 (
    .pin1(n7400_3_pin1), .pin2(n7400_3_pin2), .pin3(out_8), .pin4(n7400_3_pin4), .pin5(out_8),
    .pin6(n7400_3_pin2), .pin13(C), .pin12(clk), .pin11(n7400_3_pin1), .pin10(n7400_1_pin3), .pin9(clk),
    .pin8(n7400_3_pin4));
  _7400 u_7400_4 (
    .pin1(n7400_4_pin1), .pin2(n7400_4_pin2), .pin3(out_9), .pin4(n7400_4_pin4), .pin5(out_9),
    .pin6(n7400_4_pin2), .pin13(D), .pin12(clk), .pin11(n7400_4_pin1), .pin10(n7400_1_pin6), .pin9(clk),
    .pin8(n7400_4_pin4));

  // Notes on the sheet:
  //   d'
  //   c'
  //   a'
  //   b'
endmodule
