// Logisim project simplify with NOR.circ as structural Verilog: 1 circuit, main circuit main
module main (
  input  a,
  input  b,
  input  c,
  input  d,
  output out_5,
  output out_6
);

  wire n7402_1_pin2, n7402_1_pin10, n7402_1_pin13, n7427_1_pin6, n7427_1_pin8, n7427_1_pin12, nor_1_out,
       nor_2_out, nor_3_out, nor_4_out, nor_5_out, nor_6_out;

  _7402 u_7402_1 (
    .pin1(out_6), .pin2(n7402_1_pin2), .pin3(n7402_1_pin2), .pin13(n7402_1_pin13), .pin12(d), .pin11(d),
    .pin10(n7402_1_pin10), .pin9(a), .pin8(a));  // open: pin4, pin5, pin6
  _7427 u_7427_1 (
    .pin1(b), .pin2(d), .pin3(n7402_1_pin10), .pin4(n7402_1_pin13), .pin5(b), .pin6(n7427_1_pin6), .pin13(a),
    .pin12(n7427_1_pin12), .pin11(c), .pin10(b), .pin9(a), .pin8(n7427_1_pin8));
  nor nor_1 (nor_1_out, a, b, c);
  nor nor_2 (nor_2_out, a, b, d);
  nor nor_3 (nor_3_out, a, a);
  nor nor_4 (nor_4_out, d, d);
  nor nor_5 (nor_5_out, nor_3_out, b, nor_4_out);
  _7427 u_7427_2 (
    .pin11(n7427_1_pin8), .pin10(n7427_1_pin12), .pin9(n7427_1_pin6), .pin8(n7402_1_pin2));  // open: pin1, pin2, pin3, pin4, pin5, pin6, pin13, pin12
  nor nor_6 (nor_6_out, nor_1_out, nor_2_out, nor_5_out);
  nor nor_7 (out_5, nor_6_out, nor_6_out);
  LED led_1 (.in(out_5));

  // Notes on the sheet:
  //   1
  //   4
  //   12
  //   8
  //   6
  //   8
  //   13
endmodule
