// Logisim project half_adder.circ as structural Verilog: 1 circuit, main circuit main
module main (
  input  A1,
  input  A2,
  output S,
  output C,
  output S1,
  output C1,
  output S2,
  output C2
);

  wire n7400_1_pin3, n7400_1_pin6, n7400_1_pin11, nand_1_out, nand_2_out, nand_3_out;

  _7400 u_7400_1 (
    .pin1(A2), .pin2(A1), .pin3(n7400_1_pin3), .pin4(A2), .pin5(n7400_1_pin3), .pin6(n7400_1_pin6),
    .pin13(A1), .pin12(n7400_1_pin3), .pin11(n7400_1_pin11), .pin10(n7400_1_pin11), .pin9(n7400_1_pin6),
    .pin8(S2));
  nand nand_1 (nand_1_out, A1, A2);
  xor xor_1 (S, A1, A2);
  and and_1 (C, A1, A2);
  _7400 u_7400_2 (
    .pin1(n7400_1_pin3), .pin2(n7400_1_pin3), .pin3(C2));  // open: pin4, pin5, pin6, pin13, pin12, pin11, pin10, pin9, pin8
  nand nand_2 (nand_2_out, A1, nand_1_out);
  nand nand_3 (nand_3_out, nand_1_out, A2);
  nand nand_4 (S1, nand_2_out, nand_3_out);
  nand nand_5 (C1, nand_1_out, nand_1_out);
endmodule
