// Logisim project parity_check.circ as structural Verilog: 1 circuit, main circuit main
module main (
  input  A,
  input  B,
  input  C,
  input  D
);

  wire xor_1_out, xor_2_out, xor_3_out;

  xor xor_1 (xor_1_out, A, B);
  xor xor_2 (xor_2_out, C, D);
  xor xor_3 (xor_3_out, xor_1_out, xor_2_out);
  LED led_1 (.in(xor_3_out));
endmodule
