// Logisim project simplifying.circ as structural Verilog: 1 circuit, main circuit main
module main (
  input  A,
  input  B
);

  wire and_1_out, n7408_1_pin1, n7408_1_pin2, n7408_1_pin3, n7408_1_pin6, n7408_1_pin8, not_1_out, not_2_out,
       not_3_out, not_4_out, or_1_out, or_2_out;

  or or_1 (or_1_out, A, B);
  not not_1 (not_1_out, A);
  not not_2 (not_2_out, B);
  _7408 u_7408_1 (
    .pin1(n7408_1_pin1), .pin2(n7408_1_pin2), .pin3(n7408_1_pin3), .pin4(B), .pin5(A), .pin6(n7408_1_pin6),
    .pin10(n7408_1_pin6), .pin9(n7408_1_pin3), .pin8(n7408_1_pin8));  // open: pin13, pin12, pin11
  _7404 u_7404_1 (
    .pin1(A), .pin2(n7408_1_pin1), .pin3(B), .pin4(n7408_1_pin2));  // open: pin5, pin6, pin13, pin12, pin11, pin10, pin9, pin8
  not not_3 (not_3_out, or_1_out);
  or or_2 (or_2_out, not_1_out, not_2_out);
  and and_1 (and_1_out, not_3_out, not_4_out);
  not not_4 (not_4_out, or_2_out);
  LED led_1 (.in(and_1_out));
  LED led_2 (.in(n7408_1_pin8));
endmodule
