// Logisim project AND_XOR_with_MUX.circ as structural Verilog: 1 circuit, main circuit main
module main (
  input  a,
  input  b,
  input  a2,
  input  in_4,
  output out_5,
  output out_6
);

  wire not_1_out;

  not not_1 (not_1_out, a2);
  Multiplexer multiplexer_1 (.in0(1'b0), .in1(a), .out(out_5), .sel(b));
  Multiplexer multiplexer_2 (.in0(a2), .in1(not_1_out), .out(out_6), .sel(in_4));

  // Notes on the sheet:
  //   AND with MUX
  //   XOR with MUX
endmodule
