// Logisim project BCD_adder.circ as structural Verilog: 1 circuit, main circuit main
module main (
  input  A1,
  input  A2,
  input  A3,
  input  A4,
  input  B1,
  input  in_6,
  input  B2,
  input  B3,
  input  B4,
  input  in_10
);

  wire and_1_out, and_2_out, n74283_1_pin1, n74283_1_pin4, n74283_1_pin9, n74283_1_pin10, n74283_1_pin13,
       n74283_2_pin1, n74283_2_pin4, n74283_2_pin9, n74283_2_pin10, n74283_2_pin13, or_1_out;

  _74283 u_74283_1 (
    .pin1(n74283_1_pin1), .pin2(B2), .pin3(A2), .pin4(n74283_1_pin4), .pin5(A1), .pin6(B1), .pin15(B3),
    .pin14(A3), .pin13(n74283_1_pin13), .pin12(A4), .pin11(B4), .pin10(n74283_1_pin10), .pin9(n74283_1_pin9));  // open: pin7
  LED S1 (.in(n74283_1_pin4));
  LED S2 (.in(n74283_1_pin1));
  LED S3 (.in(n74283_1_pin13));
  LED S4 (.in(n74283_1_pin10));
  LED C0 (.in(n74283_1_pin9));
  and and_1 (and_1_out, n74283_1_pin10, n74283_1_pin13);
  and and_2 (and_2_out, n74283_1_pin10, n74283_1_pin1);
  or or_1 (or_1_out, n74283_1_pin9, and_1_out, and_2_out);
  _74283 u_74283_2 (
    .pin1(n74283_2_pin1), .pin2(or_1_out), .pin3(n74283_1_pin1), .pin4(n74283_2_pin4), .pin5(n74283_1_pin4),
    .pin6(in_6), .pin15(or_1_out), .pin14(n74283_1_pin13), .pin13(n74283_2_pin13), .pin12(n74283_1_pin10),
    .pin11(in_10), .pin10(n74283_2_pin10), .pin9(n74283_2_pin9));  // open: pin7
  LED led_1 (.in(n74283_2_pin4));
  LED led_2 (.in(n74283_2_pin1));
  LED led_3 (.in(n74283_2_pin13));
  LED led_4 (.in(n74283_2_pin10));
  LED led_5 (.in(n74283_2_pin9));
endmodule
