// Logisim project Encoder_Multiplexer.circ as structural Verilog: 1 circuit, main circuit main
module main (
  input  D0,
  input  D1,
  input  D2,
  input  D3,
  input  D4,
  input  D5,
  input  D6,
  input  D7,
  input  I0,
  input  I1,
  input  I2,
  input  I3,
  input  S1,
  input  S0,
  output out_15,
  output out_16,
  output out_17,
  output out_18
);

  wire I0_M_out, I1_M_out, I2_M_out, I3_M_out, not_1_out, not_2_out;

  not not_1 (not_1_out, S1);
  not not_2 (not_2_out, S0);
  or x (out_15, D4, D5, D6, D7);
  or y (out_16, D2, D3, D6, D7);
  or z (out_17, D7, D1, D5, D3);
  and I0_M (I0_M_out, I0, not_1_out, not_2_out);
  and I1_M (I1_M_out, I1, not_1_out, S0);
  and I2_M (I2_M_out, I2, S1, not_2_out);
  and I3_M (I3_M_out, I3, S0, S1);
  or M (out_18, I0_M_out, I1_M_out, I2_M_out, I3_M_out);

  // Notes on the sheet:
  //   Encoder
  //   Multiplexer
endmodule
