// Logisim project JK_flip_flop.circ as structural Verilog: 1 circuit, main circuit main
module main (
  input  j,
  input  k,
  output out_3,
  output out_4
);

  wire clock_1_out, j_k_ff_1_q, j_k_ff_1_qn, not_1_out;

  Clock clock_1 (.out(clock_1_out));
  J_K_Flip_Flop j_k_ff_1 (.J(j), .K(k), .clk(clock_1_out), .Q(j_k_ff_1_q), .Qn(j_k_ff_1_qn));  // open: preset, reset
  not not_1 (not_1_out, clock_1_out);
  J_K_Flip_Flop j_k_ff_2 (
    .J(j_k_ff_1_q), .K(j_k_ff_1_qn), .clk(not_1_out), .Q(out_3), .Qn(out_4));  // open: preset, reset
endmodule
