// Logisim project JK_master_slave.circ as structural Verilog: 1 circuit, main circuit main
module main (
  input  j,
  input  k,
  output Q,
  output Q_prime,
  output Q_2,
  output Q_prime_2
);

  wire clock_1_out, j_k_ff_1_q, j_k_ff_1_qn, n7400_1_pin3, n7400_1_pin6, n7400_1_pin8, n7400_1_pin11,
       n7400_1_pin12, n7400_2_pin3, n7400_2_pin6, n7400_2_pin8, n7400_2_pin11, nand_1_out, nand_2_out,
       nand_3_out, nand_4_out, nand_5_out, nand_6_out, nand_7_out;

  Clock clock_1 (.out(clock_1_out));
  _7400 u_7400_1 (
    .pin2(k), .pin3(n7400_1_pin3), .pin4(n7400_1_pin3), .pin5(clock_1_out), .pin6(n7400_1_pin6), .pin13(j),
    .pin12(n7400_1_pin12), .pin11(n7400_1_pin11), .pin10(n7400_1_pin11), .pin9(clock_1_out),
    .pin8(n7400_1_pin8));  // open: pin1
  J_K_Flip_Flop j_k_ff_1 (.J(j), .K(k), .clk(clock_1_out), .Q(j_k_ff_1_q), .Qn(j_k_ff_1_qn));  // open: preset, reset
  nand nand_1 (nand_1_out, j, Q_prime, clock_1_out);
  nand nand_2 (nand_2_out, k, Q, clock_1_out);
  nand nand_3 (nand_3_out, clock_1_out, clock_1_out);
  nand nand_4 (nand_4_out, nand_1_out, nand_5_out);
  nand nand_5 (nand_5_out, nand_4_out, nand_2_out);
  J_K_Flip_Flop j_k_ff_2 (
    .J(j_k_ff_1_q), .K(j_k_ff_1_qn), .clk(nand_3_out), .Q(Q_2), .Qn(Q_prime_2));  // open: preset, reset
  _7400 u_7400_2 (
    .pin1(n7400_1_pin6), .pin3(n7400_2_pin3), .pin4(n7400_2_pin3), .pin6(n7400_2_pin6), .pin13(n7400_1_pin8),
    .pin11(n7400_2_pin11), .pin10(n7400_2_pin11), .pin8(n7400_2_pin8));  // open: pin2, pin5, pin12, pin9
  nand nand_6 (nand_6_out, nand_4_out, nand_3_out);
  nand nand_7 (nand_7_out, nand_3_out, nand_5_out);
  _7400 u_7400_3 (
    .pin1(n7400_2_pin6), .pin13(n7400_2_pin8), .pin11(n7400_1_pin12));  // open: pin2, pin3, pin4, pin5, pin6, pin12, pin10, pin9, pin8
  nand nand_8 (Q, nand_6_out, Q_prime);
  nand nand_9 (Q_prime, Q, nand_7_out);

  // Notes on the sheet:
  //   clk
  //   JK master-slave Flip-flop
  //   k
  //   j
endmodule
