// Logisim project counters.circ as structural Verilog: 1 circuit, main circuit main
module main (
  output out_1,
  output out_2,
  output out_3,
  output out_4,
  output out_5,
  output out_6,
  output out_7,
  output out_8
);

  wire and_1_out, and_2_out, and_3_out, clock_1_out, not_1_out, not_2_out, not_3_out;

  T_Flip_Flop t_ff_1 (.T(1'b1), .clk(not_1_out), .Q(out_1));  // open: Qn, reset, preset
  T_Flip_Flop t_ff_2 (.T(and_1_out), .clk(clock_1_out), .Q(out_5));  // open: Qn, reset, preset
  and and_1 (and_1_out, out_6, and_2_out);
  T_Flip_Flop t_ff_3 (.T(1'b1), .clk(not_2_out), .Q(out_2));  // open: Qn, reset, preset
  not not_1 (not_1_out, out_2);
  T_Flip_Flop t_ff_4 (.T(and_2_out), .clk(clock_1_out), .Q(out_6));  // open: Qn, reset, preset
  and and_2 (and_2_out, and_3_out, out_7);
  T_Flip_Flop t_ff_5 (.T(1'b1), .clk(not_3_out), .Q(out_3));  // open: Qn, reset, preset
  not not_2 (not_2_out, out_3);
  T_Flip_Flop t_ff_6 (.T(and_3_out), .clk(clock_1_out), .Q(out_7));  // open: Qn, reset, preset
  and and_3 (and_3_out, 1'b1, out_8);
  Clock clock_1 (.out(clock_1_out));
  T_Flip_Flop t_ff_7 (.T(1'b1), .clk(clock_1_out), .Q(out_4));  // open: Qn, reset, preset
  not not_3 (not_3_out, out_4);
  T_Flip_Flop t_ff_8 (.T(1'b1), .clk(clock_1_out), .Q(out_8));  // open: Qn, reset, preset

  // Notes on the sheet:
  //   Asynchronus counter (ripple)
  //   Synchronus counter (binary counter)
endmodule
