// Logisim project decoder_circuit.circ as structural Verilog: 1 circuit, main circuit main
module main (
  input  a,
  input  b,
  input  c,
  output [7:0] D
);

  wire not_1_out, not_2_out, not_3_out;

  not not_1 (not_1_out, a);
  not not_2 (not_2_out, b);
  not not_3 (not_3_out, c);
  and and_1 (D[7], not_1_out, not_2_out, not_3_out);
  and and_2 (D[6], not_1_out, not_2_out, c);
  and and_3 (D[5], not_1_out, b, not_3_out);
  and and_4 (D[4], not_1_out, b, c);
  and and_5 (D[3], a, not_2_out, not_3_out);
  and and_6 (D[2], a, not_2_out, c);
  and and_7 (D[1], a, b, not_3_out);
  and and_8 (D[0], a, b, c);

  // Notes on the sheet:
  //   decoder
endmodule
