// Logisim project full subtractor.circ as structural Verilog: 1 circuit, main circuit main
module main (
  input  A,
  input  B,
  input  C,
  output dif,
  output borrow,
  output D1,
  output B1,
  output S2,
  output C2
);

  wire and_1_out, and_2_out, n7400_1_pin3, n7400_1_pin6, n7400_1_pin8, n7400_1_pin11, n7400_2_pin1,
       n7400_2_pin2, n7400_2_pin4, nand_1_out, nand_2_out, nand_3_out, nand_4_out, nand_5_out, nand_6_out,
       nand_7_out, not_1_out, not_2_out, xor_1_out;

  _7400 u_7400_1 (
    .pin1(B), .pin2(A), .pin3(n7400_1_pin3), .pin4(B), .pin5(n7400_1_pin3), .pin6(n7400_1_pin6), .pin13(A),
    .pin12(n7400_1_pin3), .pin11(n7400_1_pin11), .pin10(n7400_1_pin11), .pin9(n7400_1_pin6),
    .pin8(n7400_1_pin8));
  nand nand_1 (nand_1_out, A, B);
  not not_1 (not_1_out, A);
  xor xor_1 (xor_1_out, A, B);
  and and_1 (and_1_out, not_1_out, B);
  nand nand_2 (nand_2_out, A, nand_1_out);
  nand nand_3 (nand_3_out, nand_1_out, B);
  _7400 u_7400_2 (
    .pin1(n7400_2_pin1), .pin2(n7400_2_pin2), .pin3(S2), .pin4(n7400_2_pin4), .pin5(n7400_1_pin8),
    .pin6(n7400_2_pin2), .pin13(n7400_1_pin8), .pin12(C), .pin11(n7400_2_pin4), .pin10(n7400_2_pin4),
    .pin9(C), .pin8(n7400_2_pin1));
  not not_2 (not_2_out, xor_1_out);
  xor xor_2 (dif, xor_1_out, C);
  and and_2 (and_2_out, not_2_out, C);
  nand nand_4 (nand_4_out, nand_2_out, nand_3_out);
  _7400 u_7400_3 (
    .pin1(n7400_1_pin6), .pin2(n7400_2_pin1), .pin3(C2), .pin12(C2));  // open: pin4, pin5, pin6, pin13, pin11, pin10, pin9, pin8
  or or_1 (borrow, and_2_out, and_1_out);
  nand nand_5 (nand_5_out, nand_4_out, C);
  nand nand_6 (nand_6_out, nand_4_out, nand_5_out);
  nand nand_7 (nand_7_out, nand_5_out, C);
  nand nand_8 (D1, nand_6_out, nand_7_out);
  nand nand_9 (B1, nand_7_out, nand_3_out);
endmodule
