// Logisim project parity_bit.circ as structural Verilog: 1 circuit, main circuit main
module main (
  input  in_1,
  input  in_2,
  input  in_3,
  input  in_4,
  input  in_5,
  input  in_6,
  input  in_7,
  output out_8,
  output out_9
);

  wire xnor_1_out, xnor_2_out, xor_1_out;

  xor xor_1 (xor_1_out, in_1, in_2);
  xnor xnor_1 (xnor_1_out, in_4, in_5);
  xnor xnor_2 (xnor_2_out, in_6, in_7);
  xnor xnor_3 (out_8, xor_1_out, in_3);
  xnor xnor_4 (out_9, xnor_1_out, xnor_2_out);
endmodule
