// Logisim project sequence_detector_ic.circ as structural Verilog: 1 circuit, main circuit main
module main (
  input  I,
  output out_2
);

  wire and_1_out, and_2_out, clk_out, not_1_out, X_q, Y_q, Y_qn;

  Clock clk (.out(clk_out));
  not not_1 (not_1_out, I);
  and and_1 (and_1_out, I, Y_qn);
  and and_2 (and_2_out, X_q, not_1_out);
  D_Flip_Flop X (.D(and_1_out), .clk(clk_out), .Q(X_q));  // open: Qn, preset, reset
  D_Flip_Flop Y (.D(and_2_out), .clk(clk_out), .Q(Y_q), .Qn(Y_qn));  // open: preset, reset
  and Z (out_2, I, Y_q);

  // Notes on the sheet:
  //   sequence = 101
endmodule
