// Logisim project seven_sigment_auto.circ as structural Verilog: 1 circuit, main circuit main
module main (
  input  [3:0] i,
  output a,
  output b,
  output c,
  output d,
  output e,
  output f,
  output g
);

  wire and_1_out, and_2_out, and_3_out, and_4_out, and_5_out, and_6_out, and_7_out, and_8_out, and_9_out,
       and_10_out, and_11_out, and_12_out, and_13_out, and_14_out, and_15_out, and_16_out, not_1_out,
       not_2_out, not_3_out;

  not not_1 (not_1_out, i[2]);
  not not_2 (not_2_out, i[1]);
  not not_3 (not_3_out, i[0]);
  and and_1 (and_1_out, not_1_out, not_3_out);
  and and_2 (and_2_out, i[2], i[0]);
  and and_3 (and_3_out, not_2_out, not_3_out);
  or or_1 (b, not_1_out, and_3_out, and_4_out);
  and and_4 (and_4_out, i[1], i[0]);
  or or_2 (c, not_2_out, i[0], i[2]);
  and and_5 (and_5_out, not_1_out, not_3_out);
  and and_6 (and_6_out, not_1_out, i[1]);
  and and_7 (and_7_out, i[2], not_2_out, i[0]);
  and and_8 (and_8_out, i[1], not_3_out);
  and and_9 (and_9_out, not_1_out, not_3_out);
  or or_3 (e, and_9_out, and_10_out);
  and and_10 (and_10_out, i[1], not_3_out);
  and and_11 (and_11_out, not_2_out, not_3_out);
  and and_12 (and_12_out, i[2], not_2_out);
  and and_13 (and_13_out, i[2], not_3_out);
  and and_14 (and_14_out, not_1_out, i[1]);
  and and_15 (and_15_out, i[2], not_2_out);
  and and_16 (and_16_out, i[1], not_3_out);
  or or_4 (a, and_1_out, i[1], and_2_out, i[3]);
  or or_5 (d, and_5_out, and_6_out, and_7_out, and_8_out, i[3]);
  or or_6 (f, and_11_out, and_12_out, and_13_out, i[3]);
  or or_7 (g, and_14_out, and_15_out, i[3], and_16_out);
  _7_Segment_Display u_7_segment_display_1 (.g(g), .f(f), .a(a), .b(b), .e(e), .d(d), .c(c));  // open: dp

  // Notes on the sheet:
  //   7 segment display
endmodule
