// Logisim project xnor.circ as structural Verilog: 1 circuit, main circuit main
module main (
  input  a,
  input  b,
  input  c,
  input  d,
  output out_5
);

  wire and_1_out, and_2_out, and_3_out, and_4_out, and_5_out, and_6_out, and_7_out, and_8_out, not_1_out,
       not_2_out, not_3_out, not_4_out;

  not not_1 (not_1_out, a);
  not not_2 (not_2_out, b);
  not not_3 (not_3_out, c);
  not not_4 (not_4_out, d);
  and and_1 (and_1_out, not_1_out, not_2_out, not_3_out, not_4_out);
  and and_2 (and_2_out, not_1_out, not_2_out, c, d);
  and and_3 (and_3_out, not_1_out, b, not_3_out, d);
  and and_4 (and_4_out, not_1_out, b, c, not_4_out);
  and and_5 (and_5_out, a, not_2_out, not_3_out, d);
  and and_6 (and_6_out, a, not_2_out, c, not_4_out);
  and and_7 (and_7_out, a, b, not_3_out, not_4_out);
  and and_8 (and_8_out, a, b, c, d);
  or or_1 (out_5, and_1_out, and_2_out, and_3_out, and_4_out, and_5_out, and_6_out, and_7_out, and_8_out);

  // Notes on the sheet:
  //   xnor
endmodule
